# Fritzing sketch WaterSystem (saved by Fritzing 0.9.9b)
breadboards: 1

parts:
  Argon1 = Particle Argon
  Q1 = PNP-Transistor [package="TO92 [THT]"]
  R1 = Resistor [tolerance=±5% resistance=3.3k package="0805 [SMD]"]
  R2 = Resistor [tolerance=±5% resistance=1.5k package="0805 [SMD]"]
  OLED_I2C1 = OLED 128x64 I2C Monochrome Display
  SENS1 = SoilWatch 10
  M1 = BMP280
  Relay1 = Relay - 6 pins [package="DIP (Dual Inline) [THT]"]
  WATER_PUMP1 = water pump/motor  # not connected
  Grove1 = Grove Dust Sensor
  Part1 = MQ-131 breakout

nets:
  VCC: Argon1.3.3V, OLED_I2C1.VDD, SENS1.VCC, M1.VIN, Relay1.VCC, Part1.VCC
  GND: Argon1.GND, Q1.C, R1.Pin_0, OLED_I2C1.GND, SENS1.GND, M1.GND, Relay1.GND, Grove1.GND, Part1.GND
  N1: Argon1.A0, Part1.AO
  N2: Argon1.A5, SENS1.OUT
  N3: Argon1.RX, Q1.B, R1.Pin_1
  N4: Argon1.SDA, OLED_I2C1.SDA, M1.SDA
  N5: Argon1.SCL, OLED_I2C1.SCK, M1.SCL
  N6: Argon1.D2, Grove1.SIG
  N7: Argon1.LI+, R2.Pin_0, Relay1.ON, Grove1.VCC
  N8: Q1.E, R2.Pin_1, Relay1.IN

custom parts:
  Particle Argon: The Argon is a powerful Wi-Fi enabled development board that can act as either a standalone Wi-Fi endpoint or Wi-Fi enabled gateway for Particle Mesh networks. It is based on the Nordic nRF52840 and has built-in battery charging circuitry so it’s easy to connect a Li-Po and deploy your local network in minutes. The Argon is great for connecting existing projects to the Particle Device Cloud or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
  SoilWatch 10: SoilWatch 10 - Capacitive soil moisture sensor
  BMP280: Temperature Humidity Barometric presure Sensor, I2C
  Relay - 6 pins: A DIP stand-in part for whatever IC you want. With 6 pins on a 900mil dual inline package (DIP) footprint.
  water pump/motor: WATER PUMP BY ARDUBLOCKTR
  Grove Dust Sensor: PPD42 Grove Dust Sensor
  MQ-131 breakout: SKU: 101282
